# Fritzing sketch diagram (saved by Fritzing 0.8.7b)
breadboards: 1

parts:
  부품1 = Arduino Uno (Rev3)
  R1 = Resistor [tolerance=±5% resistance=220 package=THT]
  LED1 = LED - 5mm [color="Red (633nm)" package="5 mm [THT]"]

nets:
  N1: 부품1.D13/SCK, R1.Pin_0
  N2: 부품1.GND, LED1.anode
  N3: R1.Pin_1, LED1.cathode

notes:
  인체 감지 센서
